# Fritzing sketch wiring-11-fs3-core (saved by Fritzing 1.0.0)

parts:
  Board = Unexpected Maker FeatherS3
  J1 = Bench lines open-drain drivers
  SW1 = User key momentary, NO
  R1 = Resistor 10k
  BT1 = FeatherS3 LiPo
  U1 = BME280 STEMMA QT, 0x76
  U2 = Analog board ISO1540 side 1 (sheet 13)
  U3 = RV-8803 RTC Adafruit 6538, 0x32
  U4 = Notecarrier-X + Notecard, 0x17
  BT2 = Notecarrier LiPo

nets:
  N1: Board.RST, J1.RST
  N2: Board.IO0, J1.IO0
  GND: Board.GND, J1.GND, SW1.COM, U1.GND, U2.GND1, U3.GND, U4.GND
  N3: Board.IO1, SW1.NO, R1.2
  3V3: Board.3V3, R1.1, U3.3V3
  N4: Board.LDO2, U1.3V3, U2.VCC1
  N5: Board.SDA16, U1.SDA, U2.SDA1
  N6: Board.SCL15, U1.SCL, U2.SCL1
  N7: Board.SDA8, U3.SDA, U4.SDA
  N8: Board.SCL9, U3.SCL, U4.SCL
  N9: Board.BAT-, BT1.-
  N10: Board.BAT+, BT1.+
  N11: U4.BAT-, BT2.-
  N12: U4.BAT+, BT2.+

notes:
  FeatherS3 build: power, both buses, key and bench lines (FSD 40.2)
  Always-on bus (horizontal STEMMA QT, LDO1): RV-8803 0x32 and the Notecarrier-X 0x17,
  its red 3.3 V wire unconnected and its own LiPo. Daisy-chain through the RTC's second port.
  Switched bus (vertical STEMMA QT, LDO2, off in deep sleep): BME280 0x76 and the analog
  board's isolator (sheet 13). The board's sources give SDA = IO16, SCL = IO15 on this socket.
  User key GPIO 1 to GND, 10k pull-up to 3V3. Bench RST and GPIO 0 through open-drain
  drivers only (C-40.9). Each LiPo is charged by its own board's USB-C (C-40.11).
  Title bars: green = firmware on main; blue = in the FSD, not built yet; orange = proposed, not in the FSD.

custom parts:
  Unexpected Maker FeatherS3: Unexpected Maker FeatherS3 (ESP32-S3), the pins this project uses grouped by use, with both STEMMA QT sockets; not the physical header order.
  Bench lines open-drain drivers: The bench slot's RST and GPIO 0 lines, each through an open-drain driver (FSD C-40.9)
  User key momentary, NO: Momentary user key, normally open
  BME280 STEMMA QT, 0x76: BME280 breakout on STEMMA QT (I2C 0x76)
  Analog board ISO1540 side 1 (sheet 13): The analog board's I2C isolator, board side (sheet 13)
  RV-8803 RTC Adafruit 6538, 0x32: Adafruit RV-8803 RTC breakout (6538), STEMMA QT, I2C 0x32
  Notecarrier-X + Notecard, 0x17: Blues Notecarrier-X with Notecard on STEMMA QT, its own LiPo
