# Fritzing sketch wiring-12-fs3-displays (saved by Fritzing 1.0.0)

parts:
  Board = Unexpected Maker FeatherS3
  EPD = 4.2in e-Paper Module V2 SSD1683, 8-pin
  OLED = 3.12in OLED Ver 2.1 SSD1322, 4-wire SPI
  R1 = Resistor 10k
  U1 = Power switch Pololu 2808 (LV)
  U2 = Step-up 5 V Pololu U1V11F5

nets:
  GND: Board.GND, EPD.GND, OLED.GND, R1.2, U1.GND, U2.GND
  3V3: Board.3V3, U1.VIN
  N1: Board.IO17, U1.CTRL
  N2: Board.IO5, EPD.CS
  N3: Board.IO6, EPD.DC, OLED.DC
  N4: Board.IO7, EPD.RST
  N5: Board.IO10, EPD.BUSY
  N6: Board.IO11, OLED.CS, R1.1
  N7: Board.IO12, OLED.RES
  N8: Board.IO35, EPD.DIN, OLED.SDIN
  N9: Board.IO36, EPD.CLK, OLED.SCLK
  VCC: EPD.VCC, U1.VOUT, U2.VIN
  N10: OLED.VCC, U2.VOUT

notes:
  FeatherS3 build: e-paper and OLED on one switched supply (FSD 40.2, FR-40.4, FR-40.5)
  SPI2: SCK GPIO 36, MOSI GPIO 35 and DC GPIO 6 to both displays. E-paper CS 5, RST 7, BUSY 10;
  OLED CS 11 (10k to GND marks it fitted), RES 12. The Pololu switch takes LDO1's 3.3 V;
  GPIO 17 high turns it on, low off, then floating. Before it turns off, every display line
  is set to an input. The OLED module needs 5 V on VCC (ws-displays.md): the step-up
  is proposed, and FSD 40.2 says 3.3 V to both displays until that is amended.
  Title bars: green = firmware on main; blue = in the FSD, not built yet; orange = proposed, not in the FSD.

custom parts:
  Unexpected Maker FeatherS3: Unexpected Maker FeatherS3 (ESP32-S3), the pins this project uses grouped by use, with both STEMMA QT sockets; not the physical header order.
  4.2in e-Paper Module V2 SSD1683, 8-pin: Waveshare 4.2 inch e-Paper Module (V2), SSD1683
  3.12in OLED Ver 2.1 SSD1322, 4-wire SPI: 3.12 inch 256 x 64 OLED, SSD1322, module Ver 2.1 set for 4-wire SPI
  Power switch Pololu 2808 (LV): Pololu Mini Pushbutton Power Switch LV (#2808), the display supply
  Step-up 5 V Pololu U1V11F5: Pololu U1V11F5 5 V step-up regulator for the OLED module's VCC
