# Fritzing sketch wiring-14-fs3-serial (saved by Fritzing 1.0.0)

parts:
  Board = Unexpected Maker FeatherS3D
  U3 = Digital isolator 1 ch, 3 kV side 2 | side 1
  R1 = Resistor 100k
  U2 = Load switch
  U4 = Iso DC-DC 5 V 1 W, 3 kV
  S1 = MaxBotix MB7569-100 SCXL-MaxSonar-WRM

nets:
  GND: Board.GND, U3.GND1, R1.2, U2.GND, U4.-VIN
  N1: Board.IO14, U3.OUTA
  N2: Board.VBAT, U2.VIN
  N3: Board.IO33, U3.VCC1, R1.1, U2.ON
  N4: U3.VCC2, U4.+VO, S1.4_range, S1.6_V+
  N5: U3.INA, S1.5_TX
  N6: U3.GND2, U4.0V, S1.7_GND
  N7: U2.VOUT, U4.+VIN

notes:
  FeatherS3D build: the isolated serial port and the MaxBotix MB7569-100 (FSD 40.2, FR-40.12)
  GPIO 33 high switches the port's supply on and powers the isolator's side 1; the 100k holds it off.
  The 1 W isolated DC-DC (3 kV) gives the sensor 5 V. Its pin 5 serial output (9600 8N1, inverted
  levels) reaches UART 1 RX on GPIO 14, read inverted. Pin 4 is tied to the sensor's 5 V, so it
  ranges whenever powered; GPIO 13 (the blue LED, not on the header) stays unused. Logic levels only (C-40.4).
  Title bars: green = firmware on main; blue = in the FSD, not built yet; orange = proposed, not in the FSD.

custom parts:
  Unexpected Maker FeatherS3D: Unexpected Maker FeatherS3D (ESP32-S3), top view with USB-C up: both headers in their physical order, the STEMMA QT sockets' pins at the bottom.
  Digital isolator 1 ch, 3 kV side 2 | side 1: One-channel digital isolator, sensor to board, at least 3 kV (FSD 40.2)
  Load switch: Load switch for the loop supply: DMG2305UX P-MOSFET on a SOT-23 breakout, driven by a 2N3904
  Iso DC-DC 5 V 1 W, 3 kV: Isolated DC-DC, 5 V out, 1 W, at least 3 kV isolation (FSD 40.2)
  MaxBotix MB7569-100 SCXL-MaxSonar-WRM: MaxBotix MB7569-100 ultrasonic level sensor, serial output on pin 5
