# Fritzing sketch wiring-9-blues-sensor-bus (saved by Fritzing 1.0.0)

parts:
  Board = LilyGO T-Display-S3 AMOLED 1.91
  U9 = ADS1115 water 0x48
  J1 = Qwiic star adapter
  U1 = BME280 Qwiic, 0x76
  U13 = RV-8803 RTC Adafruit 6538, 0x32
  U2 = Notecarrier-X + Notecard MBGLW
  BT2 = Notecarrier LiPo

nets:
  N1: Board.GND_R1, U9.ADDR, U9.GND
  N2: Board.IO44, U9.SCL
  N3: Board.IO43, U9.SDA
  N4: Board.3V3_R1, U9.VDD
  GND: Board.Q_GND, J1.GND, U1.GND, U13.GND, U2.GND
  3V3: Board.Q_3V3, J1.3V3, U1.3V3, U13.3V3
  N5: Board.Q_SDA, J1.SDA, U1.SDA, U13.SDA, U2.SDA
  N6: Board.Q_SCL, J1.SCL, U1.SCL, U13.SCL, U2.SCL
  N7: U2.BAT-, BT2.-
  N8: U2.BAT+, BT2.+

notes:
  Blues build: the sensor bus, GPIO 43 SDA / 44 SCL at 100 kHz (FSD 2.2, 23, 33, 39)
  The board's Qwiic connector feeds a Qwiic star; each Qwiic board plugs into a port:
  BME280 0x76, RV-8803 RTC 0x32, Notecarrier-X 0x17 (its red 3.3 V wire unconnected,
  its own LiPo). The water probe's ADS1115 (0x48, ADDR to GND) joins the same bus
  through its 6-pin socket; its probe side is sheet 3. The BME280's pull-ups and the
  Notecard's 10k stay; cut the RTC's and the ADS1115's (bus at or above about 2.2 kOhm).
  The RTC's CR1220 keeps the time while the board is unpowered. Plug or unplug only
  with USB and the battery disconnected.
  Title bars: green = firmware on main; blue = in the FSD, not built yet; orange = proposed, not in the FSD.

custom parts:
  LilyGO T-Display-S3 AMOLED 1.91: LilyGO T-Display-S3 AMOLED 1.91 inch (ESP32-S3R8), header pins as on LilyGO's pinout picture, seen from the chip side.
  ADS1115 water 0x48: ADS1115 for the water probe, address 0x48
  Qwiic star adapter: Qwiic star adapter (e.g. SparkFun Qwiic MultiPort): every port on one I2C bus
  BME280 Qwiic, 0x76: BME280 breakout on Qwiic (I2C 0x76)
  RV-8803 RTC Adafruit 6538, 0x32: Adafruit RV-8803 RTC breakout (6538) on STEMMA QT, I2C 0x32, CR1220 backup
  Notecarrier-X + Notecard MBGLW: Blues Notecarrier-X v1.3 with Notecard Cell+WiFi NOTE-MBGLW v2.5
